# Fritzing sketch principal (saved by Fritzing 0.9.3b)
circuit board: 19.4692cm x 9.17814cm
breadboards: 1

parts:
  Rasp = Raspberry Pi Zero  # not connected
  J10 = female pin header, 13 pins [form="♀ (female)"]  # not connected
  J11 = female pin header, 12 pins [form="♀ (female)"]
  J12 = Power Jack [package=power_jack_slot]  # not connected
  J13 = female pin header, 2 pins [form="♀ (female)"]
  J14 = female pin header, 2 pins [form="♀ (female)"]
  Part1 = 16-Channel 12-bit PCA9685 PWM/Servo Driver  # not connected

nets:
  N1: J11.pin1, J11.pin2, J13.pin1
  N2: J11.pin3, J11.pin4, J13.pin2
  N3: J11.pin5, J11.pin6
  N4: J11.pin7, J11.pin8
  N5: J11.pin9, J11.pin10, J14.pin1
  N6: J11.pin11, J11.pin12, J14.pin2

custom parts:
  16-Channel 12-bit PCA9685 PWM/Servo Driver: The Adafruit 16-Channel 12-bit PWM/Servo Driver will drive up to 16 servos over I2C with only 2 pins. The on-board PCA9685 PWM controller will drive all 16 channels simultaneously with no additional processing overhead. What's more, you can chain up to 62 of them to control up to 992 servos - all with the same 2 pins
